# Fritzing sketch ProtoBot031 (saved by Fritzing 0.9.3b)
circuit board: 6.4cm x 5cm
breadboards: 1

parts:
  10K = Resistor [tolerance=±5% resistance=10k package=THT]
  220 = Resistor [tolerance=±5% resistance=220 package=THT]
  IRR = male pin header, 3 pins [form="♂ (male)"]
  IRL = male pin header, 3 pins [form="♂ (male)"]
  10K_2 = Resistor [tolerance=±5% resistance=10k package=THT]
  220_2 = Resistor [tolerance=±5% resistance=220 package=THT]
  10K_3 = Resistor [tolerance=±5% resistance=10k package=THT]
  10K_4 = Resistor [tolerance=±5% resistance=10k package=THT]
  ML = male pin header, 2 pins [form="♂ (male)"]
  Bat = male pin header, 2 pins [form="♂ (male)"]
  BL = male pin header, 2 pins [form="♂ (male)"]
  MR = male pin header, 2 pins [form="♂ (male)"]
  BR = male pin header, 2 pins [form="♂ (male)"]
  L239D = L293D [package=THT]
  USB = Arduino Nano (Rev3.0)

nets:
  N1: 10K.Pin_0, 220.Pin_0, 10K_2.Pin_0, 220_2.Pin_0, BL.pin2, BR.pin2, L239D.Enable_1, L239D.Enable_2, L239D.+V, USB.5V
  N2: 10K.Pin_1, IRR.pin2, USB.A1
  N3: 220.Pin_1, IRR.pin3
  N4: IRR.pin1, IRL.pin1, 10K_3.Pin_1, 10K_4.Pin_1, Bat.pin1, L239D.0V, USB.GND
  N5: IRL.pin2, 10K_2.Pin_1, USB.A0
  N6: IRL.pin3, 220_2.Pin_1
  N7: 10K_3.Pin_0, BR.pin1, USB.D2
  N8: 10K_4.Pin_0, BL.pin1, USB.D3
  N9: ML.pin1, L239D.Out_1_(_Controlled_by_Enable_1_)
  N10: ML.pin2, L239D.Out_2_(_Controlled_by_Enable_1_)
  N11: Bat.pin2, L239D.+Vmotor, USB.VIN
  N12: MR.pin1, L239D.Out_4_(_Controlled_by_Enable_2_)
  N13: MR.pin2, L239D.Out_3_(_Controlled_by_Enable_2_)
  N14: L239D.In_1, USB.D5
  N15: L239D.In_2, USB.D6
  N16: L239D.In_3, USB.D11/MOSI
  N17: L239D.In_4, USB.D10

notes:
  ProtoBotBoard V0.31
  github.com/Bobcatmodder/ProtoBots
  + -
  TX1
  Pwr In Gnd
